// Logisim project Simulation.circ as structural Verilog
module Sign_Calculator (
  input  [7:0] Multiplier,
  input  [7:0] Multiplicand,
  output [7:0] ABS_Multiplier,
  output Sign,
  output [7:0] ABS_Multiplicand
);

  wire [6:0] xor_2_out, xor_4_out;

  xor xor_1 (xor_2_out[1], Multiplier[1], Multiplier[7]);
  xor xor_2 (xor_2_out[0], Multiplier[0], Multiplier[7]);
  xor xor_3 (xor_4_out[1], Multiplicand[1], Multiplicand[7]);
  xor xor_4 (xor_4_out[0], Multiplicand[0], Multiplicand[7]);
  xor xor_5 (xor_2_out[2], Multiplier[2], Multiplier[7]);
  xor xor_6 (xor_4_out[2], Multiplicand[2], Multiplicand[7]);
  xor xor_7 (xor_2_out[4], Multiplier[4], Multiplier[7]);
  xor xor_8 (xor_2_out[3], Multiplier[3], Multiplier[7]);
  xor xor_9 (xor_4_out[4], Multiplicand[4], Multiplicand[7]);
  xor xor_10 (xor_4_out[3], Multiplicand[3], Multiplicand[7]);
  xor xor_11 (xor_2_out[6], Multiplier[6], Multiplier[7]);
  xor xor_12 (xor_2_out[5], Multiplier[5], Multiplier[7]);
  Adder adder_1 (.a({8{1'b0}}), .b({1'b0, xor_2_out}), .out(ABS_Multiplier), .cin(Multiplier[7]));  // open: cout
  xor xor_13 (xor_4_out[6], Multiplicand[6], Multiplicand[7]);
  xor xor_14 (xor_4_out[5], Multiplicand[5], Multiplicand[7]);
  Adder adder_2 (.a({8{1'b0}}), .b({1'b0, xor_4_out}), .out(ABS_Multiplicand), .cin(Multiplicand[7]));  // open: cout
  xor xor_15 (Sign, Multiplier[7], Multiplicand[7]);
endmodule
